# Fritzing sketch OttomoverSketch (saved by Fritzing 0.9.3b)
breadboards: 1

parts:
  part = Arduino Uno (Rev3)
  Right = IC, SIP package, 8 pins [chip_label=BTS7960]
  part_2 = IC, SIP package, 4 pins
  part_3 = DC Power [voltage=12V]
  Right_Motor = DC Motor
  Left = IC, SIP package, 8 pins [chip_label=BTS7960]
  U2 = IC, SIP package, 4 pins
  V2 = DC Power [voltage=12V]
  Left_Motor = DC Motor
  Gyro = IC, SIP package, 8 pins [chip_label=MPU6050]
  Right_sensor = IC, SIP package, 4 pins [chip_label=HC-SR04]
  Front_sensor = IC, SIP package, 4 pins [chip_label=HC-SR04]
  Left_sensor = IC, SIP package, 4 pins [chip_label=HC-SR04]

nets:
  N1: part.A5/SCL, Gyro.pin3
  N2: part.D8, Front_sensor.pin2
  N3: part.D10_PWM/SS, Right.pin2
  N4: part.D11_PWM/MOSI, Right.pin1
  N5: part.D12/MISO, Left_sensor.pin2
  N6: part.D13/SCK, Right_sensor.pin3
  N7: part.A4/SDA, Gyro.pin4
  N8: part.D2, Front_sensor.pin3
  N9: part.D4, Left_sensor.pin3
  N10: part.D5_PWM, Left.pin2
  N11: part.D6_PWM, Left.pin1
  N12: part.D7, Right_sensor.pin2
  N13: part.3V3, Gyro.pin1
  N14: part.5V, Right.pin3, Right.pin4, Right.pin7, Left.pin3, Left.pin4, Left.pin7, Right_sensor.pin4, Front_sensor.pin4, Left_sensor.pin4
  GND: Right.pin8, Left.pin8, Gyro.pin2, Right_sensor.pin1, Front_sensor.pin1, Left_sensor.pin1
  N15: part_2.pin1, part_3.V+
  N16: part_2.pin2, part_3.V-
  N17: part_2.pin3, Right_Motor.pin_2
  N18: part_2.pin4, Right_Motor.pin_1
  N19: U2.pin1, V2.V+
  N20: U2.pin2, V2.V-
  N21: U2.pin3, Left_Motor.pin_2
  N22: U2.pin4, Left_Motor.pin_1
